# Fritzing sketch hm10-2560 (saved by Fritzing 0.9.3b)
breadboards: 1

parts:
  Part1 = Bluetooth HM-10
  Part2 = Arduino Mega 2560 (Rev3)

nets:
  N1: Part1.RXD, Part2.D14/TX3
  N2: Part1.TXD, Part2.D15/RX3
  GND: Part1.GND, Part2.GND
  VCC: Part1.VCC, Part2.5V
