# Fritzing sketch hm10-Uno (saved by Fritzing 0.9.3b)
breadboards: 1

parts:
  Part2 = Arduino Uno (Rev3)
  Part5 = Bluetooth HM-10

nets:
  N1: Part2.D2, Part5.TXD
  N2: Part2.D3_PWM, Part5.RXD
  5V: Part2.5V, Part5.VCC
  GND: Part2.GND, Part5.GND
